// Logisim project circuito_cpu.circ as structural Verilog
module main (
);

  wire alu_src, and_1_out, br, clk, ctrl_unit_1_reg_write, mem_r, mem_reg, mem_w, pc_reg_alu, pc_reg_br;
  wire [2:0] alu_op;
  wire [31:0] imm_gen_1_imm, multiplexer_3_out, pc, program_mem_data, reg_file_1_reg_a_data,
       reg_file_1_reg_b_data;

  buf and_1 (and_1_out, br);  // AND_Gate
  Clock clk_src (.out(clk));
  prog_count prog_count_1 (
    .clk(clk), .imm(imm_gen_1_imm), .branch(and_1_out), .pc_reg_mux(pc_reg_br),
    .reg_in(reg_file_1_reg_a_data), .pc(pc));
  ROM #(.addrWidth(24), .dataWidth(32)) program_mem (.addr(pc[23:0]), .data(program_mem_data));
  ctrl_unit ctrl_unit_1 (
    .instr(program_mem_data), .pc_reg(pc_reg_alu), .alu_op(alu_op), .branch(br), .mem_read(mem_r),
    .mem_write(mem_w), .mem_to_reg(mem_reg), .alu_src(alu_src), .reg_write(ctrl_unit_1_reg_write),
    .pc_reg_branch(pc_reg_br));
  reg_file reg_file_1 (
    .clk(clk), .write_en(ctrl_unit_1_reg_write), .write_data(multiplexer_3_out),
    .write_addr(program_mem_data[11:7]), .reg_a_addr(program_mem_data[19:15]),
    .reg_b_addr(program_mem_data[24:20]), .reg_a_data(reg_file_1_reg_a_data),
    .reg_b_data(reg_file_1_reg_b_data));
  imm_gen imm_gen_1 (.instr(program_mem_data), .imm(imm_gen_1_imm));
  Multiplexer #(.enable("false"), .width(32)) multiplexer_1 (
    .in0(reg_file_1_reg_a_data), .in1(pc), .sel(pc_reg_alu));  // open: out
  Multiplexer #(.enable("false"), .width(32)) multiplexer_2 (
    .in0(reg_file_1_reg_b_data), .in1(imm_gen_1_imm), .sel(alu_src));  // open: out
  RAM #(.addrWidth(24), .dataWidth(32), .databus("bidir"), .enables("line"), .trigger("falling")) data_mem (
    .we(mem_w), .oe(mem_r), .clk(clk), .data(reg_file_1_reg_b_data));  // open: addr
  Multiplexer #(.enable("false"), .width(32)) multiplexer_3 (
    .in0(reg_file_1_reg_b_data), .out(multiplexer_3_out), .sel(mem_reg));  // open: in1
endmodule

// VHDL entity prog_count, as the project stores it:
library ieee;
use ieee.std_logic_1164.all;
use ieee.numeric_std.all;

entity prog_count is
    port(
        clk : in std_logic;
        imm : in std_logic_vector(31 downto 0);
        branch : in std_logic;
        pc_reg_mux : in std_logic;
        reg_in : in std_logic_vector(31 downto 0);
        pc : out std_logic_vector(31 downto 0)
    );
end prog_count;

architecture Behavioral of prog_count is
    signal immediate, ptr_pc : std_logic_vector(31 downto 0) := (others => '0');
    begin 
        immediate <= imm;
        pc <= ptr_pc;

        fetch_instr: process(clk, ptr_pc) is
        begin
            if rising_edge(clk) then
                if branch = '1' then
                	if pc_reg_mux = '1' then
                    	ptr_pc <= std_logic_vector(unsigned(ptr_pc) + unsigned(immediate));
                    else
                    	ptr_pc <= std_logic_vector(unsigned(reg_in) + unsigned(immediate));
                    end if;
                else
                    ptr_pc <= std_logic_vector(unsigned(ptr_pc) + 1);
                end if;
            end if;
        end process fetch_instr;
end Behavioral;

// VHDL entity reg_file, as the project stores it:
library ieee;
use ieee.std_logic_1164.all;
use ieee.numeric_std.all;

entity reg_file is
    port(
        clk : in std_logic;
        write_en : in std_logic;

        write_data : in std_logic_vector(31 downto 0);
        
        write_addr : in std_logic_vector(4 downto 0);
        reg_a_addr : in std_logic_vector(4 downto 0);
        reg_b_addr : in std_logic_vector(4 downto 0);

        reg_a_data : out std_logic_vector(31 downto 0);
        reg_b_data : out std_logic_vector(31 downto 0)
    );
end reg_file;

architecture Behavioral of reg_file is
    -- 32 registradores de 32 bits
    type register_mem is array (31 downto 0) of std_logic_vector(31 downto 0);
    signal register_bank : register_mem;

    begin
        register_access: process(clk) is
        begin
            -- na borda de subida
            if rising_edge(clk) then
                --  se write_en = 1, escreve no registrador
                if write_en = '1' then
                    register_bank(to_integer(unsigned(write_addr))) <= write_data;
                    reg_a_data <= (others => 'X');
                    reg_b_data <= (others => 'X');
                end if;
            elsif falling_edge(clk) then -- na borda de descida
                if write_en = '0' then -- se write_en = 0, lê do registrador
                    reg_a_data <= register_bank(to_integer(unsigned(reg_a_addr)));
                    reg_b_data <= register_bank(to_integer(unsigned(reg_b_addr)));
                end if;
            else -- se write_en = X, não faz nada
                reg_a_data <= (others => 'X');
                reg_b_data <= (others => 'X');
            end if;
        end process register_access;

end Behavioral;

// VHDL entity imm_gen, as the project stores it:
library ieee;
use ieee.std_logic_1164.all;
use ieee.numeric_std.all;

entity imm_gen is
    port(
        instr : in std_logic_vector(31 downto 0);
        imm : out std_logic_vector(31 downto 0)
    );
end imm_gen;

architecture Behavioral of imm_gen is
begin
    decode_instr : process(instr)
    begin
        -- logica para fazer decode da instrução
        case instr(6 downto 0) is
            when "0110111" => -- lui
                imm(31 downto 12) <= instr(31 downto 12);
                imm(11 downto 0) <= (others => '0');
            when "0010111" => -- auipc
                imm(31 downto 12) <= instr(31 downto 12);
                imm(11 downto 0) <= (others => '0');
            when "1101111" => -- jal
                imm(0) <= '0';
                imm(20 downto 1) <= instr(31) & instr(19 downto 12) & instr(20) & instr(30 downto 21);
                imm(31 downto 21) <= (others => instr(31));
            when "1100111" => -- jalr
                imm(11 downto 0) <= instr(31 downto 20);
                imm(31 downto 12) <= (others => instr(31));
            when "1100011" => -- branch
                imm(0) <= '0';
                imm(12 downto 1) <= instr(31) & instr(7) & instr(30 downto 25) & instr(11 downto 8);
                imm(31 downto 13) <= (others => instr(31));
            when "0000011" => -- load
                imm(11 downto 0) <= instr(31 downto 20);
                imm(31 downto 12) <= (others => instr(31));
            when "0100011" => -- store
                imm(11 downto 0) <= instr(31 downto 25) & instr(11 downto 7);
                imm(31 downto 12) <= (others => instr(31));
            when "0010011" => -- i-type
                if (instr(13) or (not instr(12))) = '1' then -- andi, ori, xori, 
                    imm(11 downto 0) <= instr(31 downto 20);
                    imm(31 downto 12) <= (others => instr(31));
                else                               -- slli e srli
                    imm(4 downto 0) <= instr(24 downto 20);
                    imm(31 downto 5) <= (others => instr(31));
                end if;
            when others => -- outros
                imm <= (others => 'X');
        end case;
    end process decode_instr;
end architecture;

// VHDL entity ctrl_unit, as the project stores it:
library ieee;
use ieee.std_logic_1164.all;


entity ctrl_unit is
    port(
        instr : in std_logic_vector(31 downto 0);
        pc_reg : out std_logic; -- 0 -> pc, 1 -> reg1
        alu_op : out std_logic_vector(2 downto 0); -- alu opcode
        branch : out std_logic; -- 0 -> não é branch e 1 -> é branch
        mem_read : out std_logic; -- 0 -> sem leitura, 1 -> leitura
        mem_write : out std_logic; -- 0 -> sem escrita, 1 -> escrita
        mem_to_reg : out std_logic; -- 0 -> alu, 1 -> mem
        alu_src : out std_logic; -- 0 -> reg, 1 -> imediato
        reg_write : out std_logic; -- 0 -> leitura , 1 -> escrita
        pc_reg_branch : out std_logic -- 0 -> pc, 1 -> reg1 (mux de entrada do somador do branch)
    );
end ctrl_unit;

architecture Behavioral of ctrl_unit is
begin
    -- alu_op           operação
    --  000     nop
    --  001     logico-aritmética (R-type)
    --  010     logico-aritmética (I-type)
    --  011     branch (equal or not equal)
    --  100     adição in1 + in2
    --  101     adição in1 + 4
    --  110     passa o imediato (in2) direto pra saída
    --  111     nop

    ctrl_decode : process(instr)
    begin
        case instr(6 downto 0) is
            when "0110011" => -- instruções tipo R
                reg_write <= '1'; -- escreve no reg
                mem_to_reg <= '0'; -- passa alu
                mem_write <= 'X';  -- não é mem
                mem_read <= 'X'; 
                branch <= '0'; -- sem branch
                alu_src <= '0'; -- reg
                alu_op <= "001"; -- (logico-aritmética)
                pc_reg <= '0'; -- passa reg
                pc_reg_branch <= '0'; -- passa pc
            when "0010011" => -- instruções tipo I
                reg_write <= '1';
                mem_to_reg <= '0'; -- passa alu
                mem_write <= 'X';  -- não é mem
                mem_read <= 'X'; 
                branch <= '0'; -- sem branch
                alu_src <= '1'; -- imediato
                alu_op <= "010"; -- (logico-aritmética)
                pc_reg <= '0'; -- passa reg
                pc_reg_branch <= '0'; -- passa pc
            when "1100011" => -- instruções de branch
                reg_write <= '0';
                mem_to_reg <= 'X'; -- não escreve em reg
                mem_write <= 'X';  -- não é mem
                mem_read <= 'X';
                branch <= '1'; -- branch
                alu_src <= '0'; -- reg
                alu_op <= "011"; -- (equal or not equal)
                pc_reg <= '0'; -- passa reg
                pc_reg_branch <= '0'; -- passa pc
            when "0010111" => -- auipc
                reg_write <= '1';
                mem_to_reg <= '0'; -- passa alu
                mem_write <= 'X';  -- não é mem
                mem_read <= 'X';
                branch <= '0'; -- sem branch
                alu_src <= '1'; -- imediato
                alu_op <= "100"; -- (add)
                pc_reg <= '1'; -- pc
                pc_reg_branch <= '0'; -- passa pc
            when "0110111" => -- lui
                reg_write <= '1';
                mem_to_reg <= '0'; -- passa alu
                mem_write <= 'X';  -- não é mem
                mem_read <= 'X';
                branch <= '0'; -- sem branch
                alu_src <= '1'; -- imediato
                alu_op <= "110"; -- (passa o imediato pra saída da ALU)
                pc_reg <= 'X'; -- essa entrada não é processada nessa alu_op
                pc_reg_branch <= '0'; -- passa pc
            when "0000011" => -- lw
                reg_write <= '1';
                mem_to_reg <= '1'; -- passa mem
                mem_write <= '0';  -- le na memória
                mem_read <= '1';
                branch <= '0'; -- sem branch
                alu_src <= '1'; -- imediato
                alu_op <= "100"; -- (add)
                pc_reg <= '0'; -- passa reg
                pc_reg_branch <= '0'; -- passa pc
            when "0100011" => -- sw
                reg_write <= '0';
                mem_to_reg <= 'X'; -- não escreve em reg
                mem_write <= '1';  -- escreve na memória
                mem_read <= '0';
                branch <= '0'; -- sem branch
                alu_src <= '1'; -- imediato
                alu_op <= "100"; -- (add)
                pc_reg <= '0'; -- passa reg
                pc_reg_branch <= '0'; -- passa pc
            when "1101111" => -- jal
                reg_write <= '1';
                mem_to_reg <= '0'; -- passa alu
                mem_write <= 'X';  -- não é mem
                mem_read <= 'X';
                branch <= '1'; -- branch
                alu_src <= '1'; -- imediato
                alu_op <= "101"; --(add + 4)
                pc_reg <= '1'; -- passa pc
                pc_reg_branch <= '0'; -- passa pc
            when "1100111" => -- jalr
                reg_write <= '1';
                mem_to_reg <= '0'; -- passa alu
                mem_write <= 'X';  -- não é mem
                mem_read <= 'X';
                branch <= '1'; -- branch
                alu_src <= '1'; -- imediato
                alu_op <= "101"; --(add + 4)
                pc_reg <= '1'; -- passa pc
                pc_reg_branch <= '1'; -- passa reg1
            when others =>
                reg_write <= 'X';
                mem_to_reg <= 'X';
                mem_write <= 'X'; 
                mem_read <= 'X';
                branch <= 'X'; 
                alu_src <= 'X'; 
                alu_op <= "XXX";
                pc_reg <= 'X'; 
                pc_reg_branch <= 'X';
        end case;
    end process ctrl_decode;
end architecture;
